# Fritzing sketch SenseoWifi-PCB (saved by Fritzing 0.9.3b)
circuit board: 3.30498cm x 7.3cm

parts:
  R5 = Resistor [tolerance=±5% resistance=150 part_number=R3 package=THT]
  R4 = Resistor [tolerance=±5% resistance=1k part_number=R2 package=THT]
  R1 = Resistor [tolerance=±5% resistance=470 part_number=R1 package=THT]
  R3 = Resistor [tolerance=±5% resistance=470 part_number=R1 package=THT]
  T1_____T2_____TP = male pin header, 3 pins [form="♂ (male)"]
  SGND = male pin header, 1 pin [form="♂ (male)"]
  LED = male pin header, 1 pin [form="♂ (male)"]
  R2 = Resistor [tolerance=±5% resistance=470 part_number=R1 package=THT]
  Buzzer = Buzzer 12mm [package=buzzer-12mm-ns-kit]
  J1 = male pin header, 8 pins [form="♂ (male)"]
  J2 = male pin header, 7 pins [form="♂ (male)"]
  WeMos_D1_Mini = WeMos D1 Mini
  TCRT = male pin header, 4 pins [form="♂ (male)"]
  PC847X = Sharp PC847X [package=THT]

nets:
  N1: R5.Pin_0, J1.pin2, WeMos_D1_Mini.D8
  N2: R5.Pin_1, Buzzer.1
  N3: R4.Pin_0, LED.pin1
  N4: R4.Pin_1, PC847X.Pin_7
  T1_OC-in: R1.Pin_0, J1.pin5, WeMos_D1_Mini.D5
  N5: R1.Pin_1, PC847X.Pin_1
  TP_OC-in: R3.Pin_0, J2.pin5, WeMos_D1_Mini.D1
  N6: R3.Pin_1, PC847X.Pin_5
  N7: T1_____T2_____TP.pin1, PC847X.Pin_16
  N8: T1_____T2_____TP.pin2, PC847X.Pin_14
  N9: T1_____T2_____TP.pin3, PC847X.Pin_12
  N10: SGND.pin1, PC847X.Pin_8, PC847X.Pin_11, PC847X.Pin_13, PC847X.Pin_15
  T2_OC-in: R2.Pin_0, J2.pin4, WeMos_D1_Mini.D2
  N11: R2.Pin_1, PC847X.Pin_3
  GND: Buzzer.2, J2.pin1, WeMos_D1_Mini.G, TCRT.pin2, PC847X.Pin_2, PC847X.Pin_4, PC847X.Pin_6, PC847X.Pin_9
  N12: J1.pin1, WeMos_D1_Mini.3V3
  LED_OC-out: J1.pin3, WeMos_D1_Mini.D7, PC847X.Pin_10
  N13: J1.pin4, WeMos_D1_Mini.D6, TCRT.pin3
  N14: J1.pin6, WeMos_D1_Mini.D0
  N15: J1.pin7, WeMos_D1_Mini.A0, TCRT.pin4
  N16: J1.pin8, WeMos_D1_Mini.RST
  N17: J2.pin2, WeMos_D1_Mini.D4
  N18: J2.pin3, WeMos_D1_Mini.D3
  N19: J2.pin6, WeMos_D1_Mini.RX
  N20: J2.pin7, WeMos_D1_Mini.TX
  N21: WeMos_D1_Mini.5V, TCRT.pin1

notes:
  Senseo Connections
  SenseoWifi - PCB v1.5
  http://github.com/ThomDietrich/SenseoWifi
  G  D4  D3  D2  D1  RX  TX
  A   D   G   V
  3V3  D8  D7  D6  D5  D0  A0  RST
  Breadboard view not used
  Check out circuit and pcb layout view
